# Fritzing sketch schema_arduino (saved by Fritzing 0.9.3b)

parts:
  Composant1 = Arduino Uno (Rev3)  # not connected
  Composant2 = Base Shield V2
  Grove_LED_Blue2 = Grove LED Blue
  Grove_LED_Blue3 = Grove LED Blue
  Grove1 = Grove Button

nets:
  N1: Composant2.pin_100, Grove1.GND
  N2: Composant2.pin_101, Grove1.VCC
  N3: Composant2.pin_102, Grove1.NC
  N4: Composant2.pin_103, Grove1.SIG
  N5: Composant2.pin_104, Grove_LED_Blue3.GND
  N6: Composant2.pin_105, Grove_LED_Blue3.NC2
  N7: Composant2.pin_106, Grove_LED_Blue3.NC1
  N8: Composant2.pin_107, Grove_LED_Blue3.SIG
  N9: Composant2.pin_108, Grove_LED_Blue2.GND
  N10: Composant2.pin_109, Grove_LED_Blue2.NC2
  N11: Composant2.pin_110, Grove_LED_Blue2.NC1
  N12: Composant2.pin_111, Grove_LED_Blue2.SIG

custom parts:
  Grove LED Blue: LED blue, Grove connector.
