# Fritzing sketch schema_arduino (saved by Fritzing 0.9.3b)

parts:
  Composant1 = Arduino Uno (Rev3)  # not connected
  Composant2 = Base Shield V2
  Grove1 = Grove Temperature Sensor

nets:
  N1: Composant2.pin_96, Grove1.GND
  N2: Composant2.pin_97, Grove1.VCC
  N3: Composant2.pin_99, Grove1.SIG
